# Fritzing sketch MainBoardRadio_v2 (saved by Fritzing 0.9.4)
breadboards: 1

parts:
  U2 = DOIT Esp32 DevKit v1 (30 pins long, 11 pins width) [part_number=ESP32S-PIN30]
  J1-GND = male pin header, 3 pins [form="♂ (male)"]
  J2-sel = male pin header, 3 pins [form="♂ (male)"]
  J3-vol = male pin header, 3 pins [form="♂ (male)"]
  J6-TFT = male pin header, 14 pins [form="♂ (male)"]
  Amplifier_TPA3116D2 = male pin header, 10 pins [form="♂ (male)"]  # not connected
  U4 = 3.5mm Audio Jack [package=audio-jack]  # not connected
  Mode_button = male pin header, 2 pins [form="♂ (male)"]
  Menu_button = male pin header, 2 pins [form="♂ (male)"]
  Snooze_btn = male pin header, 2 pins [form="♂ (male)"]
  VS1053_MP3_decoder = male pin header, 10 pins [form="♂ (male)"]
  Standby_button = male pin header, 2 pins [form="♂ (male)"]

nets:
  N1: U2.3V3, J1-GND.pin1
  N2: U2.GND, J1-GND.pin2, J6-TFT.pin2, Mode_button.pin2, Menu_button.pin2, Snooze_btn.pin2, VS1053_MP3_decoder.pin9, Standby_button.pin2
  N3: U2.D15, J6-TFT.pin3
  N4: U2.D2, J6-TFT.pin5
  N5: U2.D4, J2-sel.pin3
  N6: U2.RX2, Snooze_btn.pin1
  N7: U2.TX2, J2-sel.pin2
  N8: U2.D5, Menu_button.pin1
  N9: U2.D18, J6-TFT.pin7, VS1053_MP3_decoder.pin5
  N10: U2.D19, J6-TFT.pin9, VS1053_MP3_decoder.pin7
  N11: U2.D21, Mode_button.pin1
  N12: U2.D22, J6-TFT.pin8
  N13: U2.D23, J6-TFT.pin6, VS1053_MP3_decoder.pin6
  N14: U2.EN, J6-TFT.pin4, VS1053_MP3_decoder.pin3
  N15: U2.VP, J3-vol.pin3
  N16: U2.VN, J3-vol.pin2
  N17: U2.D34, J3-vol.pin1
  N18: U2.D35, VS1053_MP3_decoder.pin2
  N19: U2.D32, VS1053_MP3_decoder.pin8
  N20: U2.D33, Standby_button.pin1
  N21: U2.D25, VS1053_MP3_decoder.pin4
  N22: U2.D26, VS1053_MP3_decoder.pin1
  N23: U2.D13, J2-sel.pin1
  N24: U2.VIN, J1-GND.pin3, J6-TFT.pin1, VS1053_MP3_decoder.pin10

custom parts:
  DOIT Esp32 DevKit v1 (30 pins long, 11 pins width): The DOIT Esp32 DevKit v1 is one of the development board created by DOIT to evaluate the ESP-WROOM-32 module. It is based on the ESP32 microcontroller that boasts Wifi, Bluetooth, Ethernet and Low Power support all in a single chip. (vanepp) made breadboard work, adjusted pin numbering and labels and reduced size of schematic and cleaned up pcb. This chip is 30pins long (2 x15) and 11 pins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
