# Fritzing sketch SwitchBoardRadio_v6 (saved by Fritzing 0.9.4)
circuit board: 11.3cm x 3.5cm
breadboards: 3

parts:
  RE1 = Rotary Encoder [part_number=selector package=THT]
  S1 = Momentary Switch [package=tactile-pth]
  RE2 = Rotary Encoder [part_number=volume package=THT]
  S2 = Momentary Switch [package=tactile-pth]
  S3 = Momentary Switch [package=tactile-pth]
  R1 = Resistor [tolerance=±5% resistance=10k package=THT]
  R2 = Resistor [tolerance=±5% resistance=10k package=THT]
  R4 = Resistor [tolerance=±5% resistance=10k package=THT]
  J5 = male pin header, 3 pins [form="♂ (male)"]
  C1 = Capacitor [part_number=104 package=cap-pth-5mm]
  C2 = Capacitor [part_number=104 package=cap-pth-5mm]
  J6 = male pin header, 3 pins [form="♂ (male)"]
  J7 = male pin header, 3 pins [form="♂ (male)"]
  R3 = Resistor [tolerance=±5% resistance=10k package=THT]
  R10 = Resistor [tolerance=±5% resistance=10k package=THT]
  R12 = Resistor [tolerance=±5% resistance=10k package=THT]
  R7 = Resistor [tolerance=±5% resistance=10k package=THT]
  R11 = Resistor [tolerance=±5% resistance=10k package=THT]
  C4 = Capacitor [package=cap-pth-5mm]
  C5 = Capacitor [package=cap-pth-5mm]
  R14 = Resistor [tolerance=±2% resistance=10k package=THT]
  R16 = Resistor [tolerance=±2% resistance=10k package=THT]
  R17 = Resistor [tolerance=±2% resistance=10k package=THT]
  J9 = male pin header, 3 pins [form="♂ (male)"]

nets:
  N1: RE1.EncoderPinA, R1.Pin_0, R4.Pin_0
  N2: RE1.EncoderPinC, RE1.SwitchrPinD, S1.1, RE2.EncoderPinC, RE2.SwitchrPinD, S2.1, S3.1, J5.pin2, C1.2, C2.2, C4.1, C5.1
  N3: RE1.EncoderPinB, R2.Pin_0, R3.Pin_0
  N4: RE1.SwitchPinE, J6.pin1
  N5: S1.3, J9.pin3
  N6: S1.4, R14.Pin_1
  N7: RE2.EncoderPinA, R12.Pin_1
  N8: RE2.EncoderPinB, R11.Pin_1
  N9: RE2.SwitchPinE, J7.pin1
  N10: S2.3, J9.pin2
  N11: S2.4, R16.Pin_1
  N12: S3.3, J9.pin1
  N13: S3.4, R17.Pin_1
  N14: R1.Pin_1, R2.Pin_1, J5.pin3, R14.Pin_0, R16.Pin_0, R17.Pin_0
  N15: R4.Pin_1, C2.1, J6.pin3
  N16: C1.1, J6.pin2, R3.Pin_1
  N17: J7.pin2, R7.Pin_1, C5.2
  N18: J7.pin3, R10.Pin_0, C4.2
  N19: R10.Pin_1, R12.Pin_0, R7.Pin_0, R11.Pin_0

notes:
  JUNE
  v.1
  ONE
  v.6

custom parts:
  Rotary Encoder: Rotary Encoder from ALPSec11e with switch.
